# Fritzing sketch remote-control (saved by Fritzing 0.9.3b)
breadboards: 1

parts:
  Part1 = Arduino Nano (Rev3.0) (ICSP)
  Part2 = NRF24L01+ Breakout Board
  BAT1 = 18650 battery holder [package=battery-18650-kit]
  BAT2 = 18650 battery holder [package=battery-18650-kit]
  Part3 = Thumb Joystick
  Part4 = Thumb Joystick
  R1 = Trimmer Potentiometer [maximum_resistance=10kΩ package=THT]
  R2 = Trimmer Potentiometer [maximum_resistance=10kΩ package=THT]

nets:
  GND: Part1.GND, Part2.GND, BAT2.-
  N1: Part1.D2, Part3.SEL
  N2: Part1.D3, Part4.SEL
  N3: Part1.D9, Part2.CE
  N4: Part1.D10, Part2.CS
  N5: Part1.D11/MOSI, Part2.MOSI
  N6: Part1.D12/MISO, Part2.MISO
  N7: Part1.VIN, BAT1.+
  5V: Part1.5V, Part2.VCC
  N8: Part1.A5, R1.wiper
  N9: Part1.A4, R2.wiper
  N10: Part1.A3, Part4.VERT
  N11: Part1.A2, Part4.HORZ
  N12: Part1.A1, Part3.VERT
  N13: Part1.A0, Part3.HORZ
  N14: Part1.D13/SCK, Part2.SCK
  N15: BAT1.-, BAT2.+
  N16: Part3.GND, R1.leg2, R2.leg2
  N17: Part3.VCC, R1.leg1, R2.leg1

custom parts:
  18650 battery holder: 18650 Battery Holder
