# Fritzing sketch wall-e_radio (saved by Fritzing 0.9.3b)
breadboards: 1

parts:
  Part1 = Arduino Nano (Rev3.0) (ICSP)
  U1 = L9110 H-bridge module [part_number="L9110 H-bridge"]
  Part2 = NRF24L01+ Breakout Board
  DFRobot_DFPlayer_Mini1 = DFRobot DFPlayer Mini [part_number=DFR0299]
  SP1 = SPEAKER [package=pcb_mount_speaker]
  S1 = Momentary Switch [package=ksa_sealed_tac_switch]
  BAT1 = 18650 battery holder [package=battery-18650-kit]
  BAT2 = 18650 battery holder [package=battery-18650-kit]

nets:
  GND: Part1.GND, U1.GND, Part2.GND, BAT2.-
  N1: Part1.D2, Part2.CE
  N2: Part1.D4, Part2.CS
  N3: Part1.D5, U1.A-IA
  N4: Part1.D6, U1.B-IA
  N5: Part1.D7, U1.A-IB
  N6: Part1.D8, U1.B-IB
  N7: Part1.D11/MOSI, Part2.MOSI
  N8: Part1.D12/MISO, Part2.MISO
  VIN: Part1.VIN, U1.VCC, BAT1.+
  5V: Part1.5V, Part2.VCC
  N9: Part1.D13/SCK, Part2.SCK
  N10: DFRobot_DFPlayer_Mini1.SPK_1, SP1.-
  N11: DFRobot_DFPlayer_Mini1.GND-1, DFRobot_DFPlayer_Mini1.GND-2, S1.3
  N12: DFRobot_DFPlayer_Mini1.SPK_2, SP1.+
  N13: DFRobot_DFPlayer_Mini1.IO_2, S1.1
  N14: BAT1.-, BAT2.+

custom parts:
  18650 battery holder: 18650 Battery Holder
